// Logisim project Real_Alu.circ as structural Verilog: 3 circuits, main circuit In_A AND In_B
module In_A_AND_In_B (
  input  [7:0] In_A,
  input  [7:0] In_B,
  output [7:0] Alu_out
);

  assign Alu_out = In_A & In_B;  // AND_Gate and_1, 8 bits wide
endmodule

module In_a_OR_In_B (
  input  [7:0] In_A,
  input  [7:0] In_B,
  output [7:0] Alu_Out
);

  assign Alu_Out = In_A | In_B;  // OR_Gate or_1, 8 bits wide
endmodule

module Not_In_B (
  input  [7:0] In_B,
  output [7:0] Alu_Out
);

  assign Alu_Out = ~In_B;  // NOT_Gate not_1, 8 bits wide
endmodule
